# Fritzing sketch Esquema Circuito PCB Fritzing (saved by Fritzing 0.9.3b)
circuit board: 8.46667cm x 5.64444cm

parts:
  Part2 = Bluetooth HC-05 Macho
  Part3 = InvenSense MPU6050
  S1 = Pushbutton [package=THT]
  Part1 = Arduino Uno (Rev3)
  VCC1 = Battery block 9V

nets:
  N1: Part2.TXD, Part1.D0/RX
  N2: Part2.RXD, Part1.D1/TX
  VCC: Part2.VCC, Part3.VCC, Part1.5V
  GND: Part2.GND, Part3.GND, Part1.GND, VCC1.-
  N3: Part3.SCL, Part1.A5/SCL
  N4: Part3.SDA, Part3.XDA, Part3.XCL, Part3.AD0, Part1.A4/SDA
  N5: S1.leg0, VCC1.+
  N6: S1.leg1, Part1.VIN
